# Fritzing sketch UNO_DHT (saved by Fritzing 0.9.3b)
breadboards: 1

parts:
  Mod1 = KY-015 Temperature & Humidity Sensor Module [package="Breakout board"]
  元件1 = Arduino Uno (Rev3)

nets:
  N1: Mod1.S, 元件1.D8
  VIN: Mod1.Vin, 元件1.5V
  N2: Mod1.-, 元件1.GND

custom parts:
  KY-015 Temperature & Humidity Sensor Module: KY-015 temperature and humidity sensor module, provides a low-latency serial interface to measure humidity and temperature.
