# Fritzing sketch UNO_LED (saved by Fritzing 0.9.3b)
breadboards: 1

parts:
  元件1 = Arduino Uno (Rev3)
  R1 = Resistor [tolerance=±5% resistance=220 package="0603 [SMD]"]
  LED1 = smd LED [color="Red (633nm)" package="0805 [SMD]"]

nets:
  N1: 元件1.D8, R1.Pin_1
  N2: 元件1.GND, LED1.cathode
  N3: R1.Pin_0, LED1.anode
