# Fritzing sketch Ethernet_DH22 (saved by Fritzing 0.9.3b)
breadboards: 1

parts:
  元件1 = Arduino Board Ethernet
  RHT1 = Humidity and Temperature Sensor RHT03

nets:
  N1: 元件1.D8, RHT1.Data-signal
  N2: 元件1.GND, RHT1.GND_1
