# Fritzing sketch UNO_RTU_LED (saved by Fritzing 0.9.3b)
breadboards: 1

parts:
  元件1 = Arduino Ethernet Shield (Rev3)
  RS485_module1 = RS485 Module (MAX3485)
  LED1 = LED - 5mm [color="Red (633nm)" package="5 mm [THT]"]
  R1 = Resistor [tolerance=±5% resistance=220 package=THT]

nets:
  N1: 元件1.D8, R1.Pin_1
  GND: 元件1.GND, RS485_module1.GND, LED1.cathode
  N2: 元件1.RX/D0, RS485_module1.RO
  N3: 元件1.TX/D1, RS485_module1.DI
  N4: 元件1.D2, RS485_module1.RE, RS485_module1.DE
  5V: 元件1.5V, RS485_module1.VCC
  N5: LED1.anode, R1.Pin_0

custom parts:
  RS485 Module (MAX3485): Commercially available RS485 to RS232 TTL Module
