# Fritzing sketch UNO_RTU_DH22 (saved by Fritzing 0.9.3b)
breadboards: 1

parts:
  元件1 = Arduino Ethernet Shield (Rev3)
  RS485_module1 = RS485 Module (MAX3485)
  RHT1 = Humidity and Temperature Sensor RHT03

nets:
  N1: 元件1.D8, RHT1.Data-signal
  GND: 元件1.GND, RS485_module1.GND, RHT1.GND_2
  N2: 元件1.RX/D0, RS485_module1.RO
  N3: 元件1.TX/D1, RS485_module1.DI
  N4: 元件1.D2, RS485_module1.RE, RS485_module1.DE
  VCC: RS485_module1.VCC, RHT1.Vcc

custom parts:
  RS485 Module (MAX3485): Commercially available RS485 to RS232 TTL Module
