# Fritzing sketch NodeMcu_LED (saved by Fritzing 0.9.3b)
breadboards: 1

parts:
  LED1 = LED - 5mm [color="Red (633nm)" package="5 mm [THT]"]
  R1 = Resistor [tolerance=±5% resistance=220 package=THT]
  U1 = NodeMCU V3.0

nets:
  N1: LED1.cathode, U1.GND
  N2: LED1.anode, R1.Pin_0
  N3: R1.Pin_1, U1.D5

custom parts:
  NodeMCU V3.0: ESP8266 based NodeMCU
