# Fritzing sketch UNO_MQTT_LED (saved by Fritzing 0.9.3b)
breadboards: 1

parts:
  LED1 = LED - 5mm [color="Red (633nm)" package="5 mm [THT]"]
  R1 = Resistor [tolerance=±5% resistance=220 package=THT]
  元件1 = Arduino Board Ethernet

nets:
  N1: LED1.cathode, 元件1.GND
  N2: LED1.anode, R1.Pin_0
  N3: R1.Pin_1, 元件1.D8
