# Fritzing sketch UNO_BLE_LED (saved by Fritzing 0.9.3b)
breadboards: 1

parts:
  LED1 = LED - 5mm [color="Red (633nm)" package="5 mm [THT]"]
  R1 = Resistor [tolerance=±5% resistance=220 package=THT]
  元件1 = Arduino Uno (Rev3)
  元件2 = Bluetooth HC-05 Macho

nets:
  GND: LED1.cathode, 元件1.GND, 元件2.GND
  N1: LED1.anode, R1.Pin_0
  N2: R1.Pin_1, 元件1.D8
  N3: 元件1.D10_PWM/SS, 元件2.TXD
  N4: 元件1.D11_PWM/MOSI, 元件2.RXD
  5V: 元件1.5V, 元件2.VCC
