# Fritzing sketch UNO_BLE_DH22 (saved by Fritzing 0.9.3b)
breadboards: 1

parts:
  元件1 = Arduino Uno (Rev3)
  元件2 = Bluetooth HC-05 Macho
  RHT1 = Humidity and Temperature Sensor RHT03

nets:
  N1: 元件1.D10_PWM/SS, 元件2.TXD
  N2: 元件1.D11_PWM/MOSI, 元件2.RXD
  VCC: 元件1.5V, 元件2.VCC, RHT1.Vcc
  GND: 元件1.GND, 元件2.GND
