# Fritzing sketch NodeMCU_RESTAPI_DHT22 (saved by Fritzing 0.9.3b)
breadboards: 1

parts:
  U1 = NodeMCU V3.0
  DHT1 = DHT22 Humidity and Temperature Sensor

nets:
  N1: U1.GND#6, U1.GND#13, U1.GND#16, U1.GND#33, DHT1.GND
  N2: U1.D5, DHT1.DATA
  VIN: U1.Vin, DHT1.VDD

custom parts:
  NodeMCU V3.0: ESP8266 based NodeMCU
