# Fritzing sketch RFID (saved by Fritzing 0.9.3b)
breadboards: 1

parts:
  U1 = NodeMCU V3.0
  元件1 = RFID-RC522-v2
  J1 = Piezo Speaker
  元件2 = LCD1602-I2C
  KF-1 = KF-301 Relay [package=THT]
  KF-2 = KF-301 Relay [package=THT]
  LED1 = smd LED [color="Red (633nm)" package="0603 [SMD]"]
  LED2 = smd LED [color="Green (565nm)" package="1206 [SMD]"]
  R1 = Resistor [tolerance=±5% resistance=220 package="0805 [SMD]"]
  R2 = Resistor [tolerance=±5% resistance=220 package="0805 [SMD]"]

nets:
  N1: U1.D1, 元件2.SCL
  N2: U1.D2, 元件2.SDA
  N3: U1.D3, 元件1.RST
  N4: U1.D4, 元件1.SDA
  3V3: U1.3V3, 元件1.3.3V
  GND: U1.GND#6, U1.GND#13, U1.GND#16, U1.GND#33, 元件1.GND, J1.pin1, 元件2.GND, KF-1.ground, KF-2.ground, LED1.cathode, LED2.cathode
  N5: U1.D5, 元件1.SCK
  N6: U1.D6, 元件1.MISO
  N7: U1.D7, 元件1.MOSI
  N8: U1.D8, J1.pin2
  N9: U1.RX, KF-1.signal
  N10: U1.TX, KF-2.signal
  VIN: U1.Vin, 元件2.VCC, KF-1.power, KF-1.NC, KF-2.power, KF-2.NC
  N11: KF-1.C, R2.Pin_0
  N12: KF-2.C, R1.Pin_1

custom parts:
  NodeMCU V3.0: ESP8266 based NodeMCU
  RFID-RC522-v2: A simple China made RFID-RC522 Reader; do check the pin labels, as this is a MFRC522 based clone.
  LCD1602-I2C: A standard character display, usually with 2x16 characters. Comes in many colors with LCM1602 IIC attached.
  KF-301 Relay: KF-301
