# Fritzing sketch Arm (saved by Fritzing 0.9.3b)

parts:
  M1 = Stepper Motor - Bipolar
  元件1 = Arduino Mega 2560 (Rev3)
  元件2 = Arduino Ethernet Shield (Rev3)  # not connected
  Arduino_CNC_Shield_V3_00_1 = Arduino_CNC_V3.00
  M2 = Stepper Motor - Bipolar
  M3 = Stepper Motor - Bipolar
  Power_plug1 = Power plug
  J1 = Basic Servo
  元件3 = Arduino Mega 2560 (Rev3)  # not connected
  元件4 = Arduino Ethernet Shield (Rev3)  # not connected
  Arduino_CNC_Shield_V3_00_2 = Arduino_CNC_V3.00
  Power_plug2 = Power plug
  M4 = Stepper Motor - Bipolar

nets:
  N1: M1.A, Arduino_CNC_Shield_V3_00_1.X-MTR_'4'
  N2: M1.C, Arduino_CNC_Shield_V3_00_1.X-MTR_'3'
  N3: M1.B, Arduino_CNC_Shield_V3_00_1.X-MTR_'2'
  N4: M1.D, Arduino_CNC_Shield_V3_00_1.X-MTR_'1'
  5V: 元件1.5V, J1.vcc
  N5: 元件1.D22, J1.pulse
  GND: 元件1.GND, J1.gnd
  N6: Arduino_CNC_Shield_V3_00_1.POWER_-, Power_plug1.GND
  N7: Arduino_CNC_Shield_V3_00_1.POWER_+, Power_plug1.VCC
  N8: Arduino_CNC_Shield_V3_00_1.Z-MTR_'1', M2.D
  N9: Arduino_CNC_Shield_V3_00_1.Z-MTR_'2', M2.B
  N10: Arduino_CNC_Shield_V3_00_1.Z-MTR_'3', M2.C
  N11: Arduino_CNC_Shield_V3_00_1.Z-MTR_'4', M2.A
  N12: Arduino_CNC_Shield_V3_00_1.Y-MTR_'1', M3.D
  N13: Arduino_CNC_Shield_V3_00_1.Y-MTR_'2', M3.B
  N14: Arduino_CNC_Shield_V3_00_1.Y-MTR_'3', M3.C
  N15: Arduino_CNC_Shield_V3_00_1.Y-MTR_'4', M3.A
  N16: Arduino_CNC_Shield_V3_00_2.POWER_-, Power_plug2.GND
  N17: Arduino_CNC_Shield_V3_00_2.POWER_+, Power_plug2.VCC
  N18: Arduino_CNC_Shield_V3_00_2.X-MTR_'1', M4.D
  N19: Arduino_CNC_Shield_V3_00_2.X-MTR_'2', M4.B
  N20: Arduino_CNC_Shield_V3_00_2.X-MTR_'3', M4.C
  N21: Arduino_CNC_Shield_V3_00_2.X-MTR_'4', M4.A

notes:
  X Axis
  Y Axis
  Z Axis
  A Axis
  Craw Servo

custom parts:
  Arduino_CNC_V3.00: Protoneer Arduino CNC Shield V3.00 If using Grbl V0.9: The “A” axis can not be used (yet). The “SCL” (Arduino A5) pin is now used for 'Probing' input. The “End Stops Z+ & Z-” (Arduino D11) and “SpnEn” (Arduino D12) have been switched!
