# Fritzing sketch ESP32_Stepper (saved by Fritzing 0.9.3b)

parts:
  U1 = ESP32S-HiLetgo [part_number=ESP32S-HiLetgo]
  Driver1 = 28BYJ-48 Driver Module [part_number=ULN2003 package=THT]
  SM1 = 28BYJ-48 Stepper Motor [part_number=28BYJ-48]
  Driver2 = 28BYJ-48 Driver Module [part_number=ULN2003 package=THT]
  SM2 = 28BYJ-48 Stepper Motor [part_number=28BYJ-48]
  Power_plug1 = Power plug

nets:
  N1: U1.GPIO32, Driver2.IN1
  N2: U1.GPIO33, Driver2.IN2
  N3: U1.GPIO25, Driver2.IN3
  N4: U1.GPIO26, Driver2.IN4
  N5: U1.GPIO16, Driver1.IN1
  N6: U1.GPIO17, Driver1.IN2
  N7: U1.GPIO18, Driver1.IN3
  N8: U1.GPIO19, Driver1.IN4
  GND: Driver1.GND, Driver2.GND, Power_plug1.GND
  N9: Driver1.Vmotor, Driver2.Vmotor, Power_plug1.VCC
  N10: Driver1.blue-pin, SM1.blue-pin
  N11: Driver1.pink-pin, SM1.pink-pin
  N12: Driver1.yellow-pin, SM1.yellow-pin
  N13: Driver1.orange-pin, SM1.orange-pin
  N14: Driver1.red-pin, SM1.red-pin
  N15: Driver2.blue-pin, SM2.blue-pin
  N16: Driver2.pink-pin, SM2.pink-pin
  N17: Driver2.yellow-pin, SM2.yellow-pin
  N18: Driver2.orange-pin, SM2.orange-pin
  N19: Driver2.red-pin, SM2.red-pin

custom parts:
  ESP32S-HiLetgo: HiLetgo ESP-WROOM-32 ESP32 ESP-32S Development Board 2.4GHz Dual-Mode WiFi + Bluetooth Dual Cores Microcontroller The ESP32 integrated with Antenna switches, RF Balun, power amplifiers, low-noise amplifiers, filters, and management modules, and the entire solution occupies the least area of PCB. 2.4 GHz Wi-Fi plus Bluetooth dual-mode chip, with TSMC Ultra-low power consumption 40nm technology,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
  28BYJ-48 Driver Module: ULN2003 Driver Module for the 28BYJ-48 Unipolar Stepper Motor LED A - Blue wire - Bottom coil left LED B - Pink wire - Top coil left LED C - Yellow wire - Bottom coil right LED D - Orange wire - Top coil right Common rail - red Connector pins: blue - pink - yellow - orange - red Control pins - IN1 to IN4 Power pins - GND & Vmotor (5-12V) On/Off jumper (if removed, power to motor is cut).
  28BYJ-48 Stepper Motor: Unipolar Stepper Motor 28BYJ-48 Top coil - pink & orange Bottom coil - blue & yellow Common rail - red Connector pins: blue - pink - yellow - orange - red
