# Fritzing sketch ModbusTCP_PMS5003ST (saved by Fritzing 0.9.3b)

parts:
  U1 = Hirose DF13 Series Header [part_number=DF13#-8P-1.25V package=DF13C-8P-1.25V]
  U2 = ESP32S-HiLetgo [part_number=ESP32S-HiLetgo]

nets:
  N1: U1.1, U2.VIN
  N2: U1.2, U2.GPIO11
  N3: U1.4, U2.GPIO17
  N4: U1.5, U2.GPIO16

custom parts:
  ESP32S-HiLetgo: HiLetgo ESP-WROOM-32 ESP32 ESP-32S Development Board 2.4GHz Dual-Mode WiFi + Bluetooth Dual Cores Microcontroller The ESP32 integrated with Antenna switches, RF Balun, power amplifiers, low-noise amplifiers, filters, and management modules, and the entire solution occupies the least area of PCB. 2.4 GHz Wi-Fi plus Bluetooth dual-mode chip, with TSMC Ultra-low power consumption 40nm technology,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
